# Fritzing sketch wemos-soil (saved by Fritzing 0.9.3b)
breadboards: 1

parts:
  WeMos_D1_Mini1 = WeMos D1 Mini
  Soil_Moisture_sensor = DFRobot Capacitive Soil Moisture Sensor V1.0 [part_number=SEN0193]

nets:
  5V: WeMos_D1_Mini1.5V, Soil_Moisture_sensor.VCC
  N1: WeMos_D1_Mini1.A0, Soil_Moisture_sensor.A
  N2: WeMos_D1_Mini1.G, Soil_Moisture_sensor.GND

custom parts:
  DFRobot Capacitive Soil Moisture Sensor V1.0: DFRobot Capacitive Soil Moisture Sensor V1.0 This product measures soil moisture levels by capacitive sensing, rather than resistive sensing like other types of moisture sensor. It is made of a corrosion resistant material giving it a long service life. Insert it into soil and impress your friends with the real-time soil moisture data! The product includes an on-board voltage regulator which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
